# Fritzing sketch OpenClaw (saved by Fritzing 1.0.3)
breadboards: 1

parts:
  Arduino_Uno = Arduino Uno (Rev3)
  CDS_(photoresistor) = Photocell (LDR) [package=THT]
  10k_(CDS_divider) = Resistor [resistance=10k package=THT]
  RGB_LED_-_R = Red LED - 5mm [package="5 mm [THT]"]
  220R_(R) = Resistor [resistance=220 package=THT]
  RGB_LED_-_G = Red LED - 5mm [package="5 mm [THT]"]
  220R_(G) = Resistor [resistance=220 package=THT]
  RGB_LED_-_B = Red LED - 5mm [package="5 mm [THT]"]
  220R_(B) = Resistor [resistance=220 package=THT]
  Button_-_ALARM = Pushbutton [package=THT]
  Button_-_LIGHT = Pushbutton [package=THT]
  Servo_-_PC_power = Basic Servo
  Servo_-_room_light = Basic Servo
  Piezo_Buzzer = LilyPad Buzzer

nets:
  N1: Arduino_Uno.A0, CDS_(photoresistor).pin_1, 10k_(CDS_divider).Pin_0
  VCC: Arduino_Uno.5V, CDS_(photoresistor).pin_0, Servo_-_PC_power.vcc, Servo_-_room_light.vcc
  GND: Arduino_Uno.GND, 10k_(CDS_divider).Pin_1, RGB_LED_-_R.cathode, RGB_LED_-_G.cathode, RGB_LED_-_B.cathode, Button_-_ALARM.leg0, Button_-_LIGHT.leg0, Servo_-_PC_power.gnd, Servo_-_room_light.gnd, Piezo_Buzzer.-
  N2: Arduino_Uno.D8, Piezo_Buzzer.+
  N3: Arduino_Uno.D9_PWM, Servo_-_PC_power.pulse
  N4: Arduino_Uno.D10_PWM/SS, Servo_-_room_light.pulse
  N5: Arduino_Uno.D3_PWM, 220R_(R).Pin_1
  N6: Arduino_Uno.D4, Button_-_ALARM.leg1
  N7: Arduino_Uno.D5_PWM, 220R_(G).Pin_1
  N8: Arduino_Uno.D6_PWM, 220R_(B).Pin_1
  N9: Arduino_Uno.D7, Button_-_LIGHT.leg1
  N10: RGB_LED_-_R.anode, 220R_(R).Pin_0
  N11: RGB_LED_-_G.anode, 220R_(G).Pin_0
  N12: RGB_LED_-_B.anode, 220R_(B).Pin_0
